# Fritzing sketch Wiring Diagram (saved by Fritzing 0.9.3b)
breadboards: 1

parts:
  Raspberry_Pi_A1 = Raspberry Pi A
  U1 = JOYSTICK-PSP1000 [package=joystick-psp1000]
  Raspberry_Pi_1 = Raspberry Pi 3 [part_number=RPI-3-V1.2]  # not connected

nets:
  GND: Raspberry_Pi_A1.GND, U1.GND

notes:
  joystick
  Topside Computer
  USB
  QGroundControl
