# Fritzing sketch WiringDiagram (saved by Fritzing 0.9.3b)
breadboards: 1

parts:
  BAT1 = Battery Holders [package=lipo-1100mAh]
  S2 = SPST Switch [package=switch-spdt_kit]
  F1 = FUSE [package=fuse_5mm]
  BeagleBone1 = BeagleBone Black
  Part1 = Logic Level Converter
  Part2 = Arduino Mega 2560 (Rev3)
  Part3 = ESC MLF1218
  MOTOR1 = Vibration Motor
  Part4 = ESC MLF1218
  MOTOR2 = Vibration Motor
  Part5 = ESC MLF1218
  MOTOR3 = Vibration Motor
  Part6 = ESC MLF1218
  MOTOR4 = Vibration Motor
  Part7 = ESC MLF1218
  MOTOR5 = Vibration Motor
  Part8 = ESC MLF1218
  MOTOR6 = Vibration Motor

nets:
  N1: BAT1.+, S2.O
  N2: BAT1.-, Part1.RX_HV
  N3: S2.P, S2.S
  N4: F1.1, Part1.TX2_HV, Part2.D15/RX3
  N5: BeagleBone1.no_name_yet#1, Part1.LV
  GND: BeagleBone1.no_name_yet#3, Part1.GND, Part2.GND
  N6: BeagleBone1.no_name_yet#19, Part8.+5
  N7: BeagleBone1.no_name_yet#20, Part8.PPM
  N8: BeagleBone1.no_name_yet#21, Part3.+5
  N9: BeagleBone1.no_name_yet#22, Part3.PPM
  N10: BeagleBone1.no_name_yet#33, BeagleBone1.no_name_yet#35, Part1.TX2_LV
  N11: BeagleBone1.no_name_yet#34, BeagleBone1.no_name_yet#36, Part1.RX2_LV
  N12: Part1.HV, Part2.5V
  N13: Part1.RX2_HV, Part2.D14/TX3
  N14: Part3.GND, MOTOR1.NEG
  N15: Part3.V+, MOTOR1.POS
  N16: Part4.GND, MOTOR2.NEG
  N17: Part4.V+, MOTOR2.POS
  N18: Part5.GND, MOTOR3.NEG
  N19: Part5.V+, MOTOR3.POS
  N20: Part6.GND, MOTOR4.NEG
  N21: Part6.V+, MOTOR4.POS
  N22: Part7.GND, MOTOR5.NEG
  N23: Part7.V+, MOTOR5.POS
  N24: Part8.GND, MOTOR6.NEG
  N25: Part8.V+, MOTOR6.POS

custom parts:
  BeagleBone Black: BeagleBone Black rev. A5B
  ESC MLF1218: ESC (Electronic Speed Control) for Cheerson CX-20 quadcopter
  Vibration Motor: An eccentric vibration motor!
